// Digital circuit fib1.dig as structural Verilog
module fib1 (
  input  [7:0] n,
  input  [7:0] f0,
  input  [7:0] f1,
  input  reset,
  input  start,
  input  clock,
  output [7:0] result,
  output finish
);

  wire comparator_1_eq, fib_controller_1_cont_load, fib_controller_1_f0_load, fib_controller_1_f0_sel,
       fib_controller_1_f1_load, fib_controller_1_f1_sel, fib_controller_1_n_load, fib_controller_1_n_sel,
       fib_controller_1_res_load, fib_controller_1_temp_load;
  wire [7:0] add_1_s, continue_q, f0_q, f1_q, fib_controller_1_state, multiplexer_1_out, multiplexer_2_out,
       multiplexer_3_out, n_q, sub_s, temp_q;

  fib_controller fib_controller_1 (
    .clk(clock), .rst(reset), .start(start), .neq0(comparator_1_eq), .\continue (continue_q),
    .finish(finish), .n_sel(fib_controller_1_n_sel), .n_load(fib_controller_1_n_load),
    .res_load(fib_controller_1_res_load), .f0_sel(fib_controller_1_f0_sel),
    .f0_load(fib_controller_1_f0_load), .f1_sel(fib_controller_1_f1_sel), .f1_load(fib_controller_1_f1_load),
    .temp_load(fib_controller_1_temp_load), .cont_load(fib_controller_1_cont_load),
    .state(fib_controller_1_state));
  Comparator #(.Bits(8)) comparator_1 (.a(n_q), .b({8{1'b0}}), .eq(comparator_1_eq));  // open: gt, lt
  // Probe on fib_controller_1_state
  Multiplexer #(.Bits(8)) multiplexer_1 (.sel(fib_controller_1_n_sel), .in_0(sub_s), .in_1(n), .out(multiplexer_1_out));
  Multiplexer #(.Bits(8)) multiplexer_2 (
    .sel(fib_controller_1_f1_sel), .in_0(f1), .in_1(add_1_s), .out(multiplexer_2_out));
  Multiplexer #(.Bits(8)) multiplexer_3 (
    .sel(fib_controller_1_f0_sel), .in_0(f0), .in_1(f1_q), .out(multiplexer_3_out));
  Register #(.Bits(8)) u_n (.D(multiplexer_1_out), .C(clock), .en(fib_controller_1_n_load), .Q(n_q));
  Register #(.Bits(8)) u_f1 (.D(multiplexer_2_out), .C(clock), .en(fib_controller_1_f1_load), .Q(f1_q));
  Register #(.Bits(8)) \continue  (.D(8'h5), .C(clock), .en(fib_controller_1_cont_load), .Q(continue_q));
  Register #(.Bits(8)) u_f0 (.D(multiplexer_3_out), .C(clock), .en(fib_controller_1_f0_load), .Q(f0_q));
  Sub #(.Bits(8)) sub (.a(n_q), .b(8'h1), .c_i(1'b0), .s(sub_s));  // open: c_o
  Add #(.Bits(8)) add_1 (.a(f1_q), .b(temp_q), .c_i(1'b0), .s(add_1_s));  // open: c_o
  Register #(.Bits(8)) res (.D(f0_q), .C(clock), .en(fib_controller_1_res_load), .Q(result));
  Register #(.Bits(8)) temp (.D(f0_q), .C(clock), .en(fib_controller_1_temp_load), .Q(temp_q));

  // Notes on the sheet:
  //   clock: Hz: 50
endmodule
