// Digital circuit fib_controller.dig as structural Verilog
module fib_controller (
  input  clk,
  input  rst,
  input  start,
  input  neq0,
  input  [7:0] \continue ,
  output finish,
  output [7:0] state,
  output n_sel,
  output n_load,
  output res_load,
  output f0_sel,
  output f0_load,
  output f1_sel,
  output f1_load,
  output temp_load,
  output cont_load
);

  controller #(.applicationType("IVERILOG")) u_controller (
    .clk(clk), .rst(rst), .start(start), .neq0(neq0), .cont(\continue ), .finish(finish), .sel_n(n_sel),
    .load_n(n_load), .load_result(res_load), .sel_f0(f0_sel), .load_f0(f0_load), .sel_f1(f1_sel),
    .load_f1(f1_load), .load_temp(temp_load), .load_cont(cont_load), .state(state));
endmodule

/* Code of controller:
module controller(clk, rst, start,neq0, cont,
	finish, sel_n, load_n,load_result,
	sel_f0, load_f0,sel_f1,load_f1,load_temp,load_cont,
	state
	);
	input clk, rst, start, neq0;
	input [7:0] cont;

	output finish,sel_n,load_n,load_result,sel_f0,load_f0,sel_f1,load_f1,load_temp,load_cont;
	output [7:0] state;
	reg [7:0] state, next_state;

	always @(posedge clk)
	begin
		if(rst)
			state = 8'd0;
		else
			state = next_state;
	end

	assign finish = (state == 8'd5) ? 1 : 0;	
	assign sel_n = (state == 0) ? 1:
			(state == 2) ?0:0;
	assign load_n = (state==0||state==2)?1:0;
	
	assign load_result = (state==4) ? 1 : 0;

	assign load_temp=(state==2)?1:0;

	assign sel_f0=(state==0)?0:
			(state==2)?1:1;
	assign load_f0=(state==0||state==2)?1:0;
	
	assign sel_f1=(state==0)?0:
			(state==3)?1:1;
	assign load_f1=(state==0||state==3)?1:0;
	
	
	
	assign load_cont=(state==0)?1:0;

	

	
	always @(state or start or neq0 or cont)
	begin
		case(state)
			8'd0: if(start)
				next_state = 8'd1;
			      else
				next_state = 8'd0;
			8'd1: if(neq0) 
				next_state = 8'd4;
			      else
				next_state = 8'd2;
			8'd2:
				next_state = 8'd3;
			8'd3:
				next_state = 8'd1;

			8'd4:
				next_state = cont;
			8'd5:
				next_state = 8'd5;
			default: next_state = 8'd0;
		endcase
	end
	
endmodule
*/
