// Digital circuit fib.dig as structural Verilog
module fib (
  input  [7:0] input_n,
  input  reset,
  input  start,
  input  clock,
  output Finish,
  output [7:0] Result,
  output [7:0] n
);

  wire comparator_1_lt, fib_controller_1_continue_load, fib_controller_1_n_load, fib_controller_1_res_load,
       fib_controller_1_res_sel, fib_controller_1_stack1_pop, fib_controller_1_stack1_push,
       fib_controller_1_stack2_pop, fib_controller_1_stack2_push, stack1_state_or_n_empty,
       stack2_res_temp_empty;
  wire [1:0] fib_controller_1_continue_sel, fib_controller_1_n_sel, fib_controller_1_stack_sel;
  wire [7:0] Add_s, continue_q, fib_controller_1_state, multiplexer_1_out, multiplexer_2_out,
       multiplexer_3_out, multiplexer_4_out, stack1_state_or_n_dout, stack2_res_temp_dout, Sub_2_s, Sub_s;

  fib_controller fib_controller_1 (
    .clk(clock), .rst(reset), .start(start), .nless2(comparator_1_lt), .\continue (continue_q),
    .finish(Finish), .n_load(fib_controller_1_n_load), .res_load(fib_controller_1_res_load),
    .res_sel(fib_controller_1_res_sel), .continue_load(fib_controller_1_continue_load),
    .stack1_push(fib_controller_1_stack1_push), .stack1_pop(fib_controller_1_stack1_pop),
    .stack2_push(fib_controller_1_stack2_push), .stack2_pop(fib_controller_1_stack2_pop),
    .n_sel(fib_controller_1_n_sel), .stack_sel(fib_controller_1_stack_sel),
    .continue_sel(fib_controller_1_continue_sel), .state(fib_controller_1_state));
  // Probe on fib_controller_1_state
  Multiplexer #(.Selector_Bits(2), .Bits(8)) multiplexer_1 (
    .sel(fib_controller_1_n_sel), .in_0(input_n), .in_1(stack1_state_or_n_dout), .in_2(Sub_s),
    .in_3({8{1'b0}}), .out(multiplexer_1_out));
  Multiplexer #(.Selector_Bits(2), .Bits(8)) multiplexer_2 (
    .sel(fib_controller_1_continue_sel), .in_0(8'h5), .in_1(8'h6), .in_2(8'h8),
    .in_3(stack1_state_or_n_dout), .out(multiplexer_2_out));
  Register #(.Bits(8)) u_n (.D(multiplexer_1_out), .C(clock), .en(fib_controller_1_n_load), .Q(n));
  Register #(.Bits(8)) \continue  (
    .D(multiplexer_2_out), .C(clock), .en(fib_controller_1_continue_load), .Q(continue_q));
  Sub #(.Bits(8)) Sub (.a(n), .b(8'h1), .c_i(1'b0), .s(Sub_s));  // open: c_o
  Multiplexer #(.Bits(8)) multiplexer_3 (
    .sel(fib_controller_1_res_sel), .in_0(Add_s), .in_1(n), .out(multiplexer_3_out));
  Comparator #(.Bits(8)) comparator_1 (.a(n), .b(8'h2), .lt(comparator_1_lt));  // open: gt, eq
  Sub #(.Bits(8)) Sub_2 (.a(n), .b(8'h2), .c_i(1'b0), .s(Sub_2_s));  // open: c_o
  Register #(.Bits(8)) res (.D(multiplexer_3_out), .C(clock), .en(fib_controller_1_res_load), .Q(Result));
  Multiplexer #(.Selector_Bits(2), .Bits(8)) multiplexer_4 (
    .sel(fib_controller_1_stack_sel), .in_0(n), .in_1(continue_q), .in_2(Sub_2_s), .in_3({8{1'b0}}),
    .out(multiplexer_4_out));
  stack stack1_state_or_n (
    .clk(clock), .rst(reset), .push(fib_controller_1_stack1_push), .pop(fib_controller_1_stack1_pop),
    .din(multiplexer_4_out), .empty(stack1_state_or_n_empty), .dout(stack1_state_or_n_dout));  // open: full, top_num
  stack stack2_res_temp (
    .clk(clock), .rst(reset), .push(fib_controller_1_stack2_push), .pop(fib_controller_1_stack2_pop),
    .din(Result), .empty(stack2_res_temp_empty), .dout(stack2_res_temp_dout));  // open: full, top_num
  // Probe on stack1_state_or_n_empty
  // Probe on stack2_res_temp_empty
  Add #(.Bits(8)) Add (.a(Result), .b(stack2_res_temp_dout), .c_i(1'b0), .s(Add_s));  // open: c_o

  // Notes on the sheet:
  //   clock: Hz: 100
endmodule
