// Digital circuit fib_controller.dig as structural Verilog
module fib_controller (
  input  clk,
  input  rst,
  input  start,
  input  nless2,
  input  [7:0] \continue ,
  output finish,
  output [7:0] state,
  output n_load,
  output res_load,
  output res_sel,
  output continue_load,
  output stack1_push,
  output stack1_pop,
  output stack2_push,
  output stack2_pop,
  output [1:0] n_sel,
  output [1:0] stack_sel,
  output [1:0] continue_sel
);

  controller #(.applicationType("IVERILOG")) u_controller (
    .clk(clk), .rst(rst), .start(start), .nless2(nless2), .cont(\continue ), .finish(finish),
    .load_n(n_load), .load_result(res_load), .sel_result(res_sel), .load_continue(continue_load),
    .stack1_push(stack1_push), .stack1_pop(stack1_pop), .stack2_push(stack2_push), .stack2_pop(stack2_pop),
    .sel_n(n_sel), .sel_stack1(stack_sel), .sel_continue(continue_sel), .state(state));
endmodule

/* Code of controller:
module controller(clk, rst, start, nless2, cont,
	finish, sel_n, load_n, sel_result,load_result,
	sel_continue, load_continue,sel_stack1,stack1_push,stack1_pop,
	stack2_push,stack2_pop,state);
	input clk, rst, start, nless2;
	input [7:0] cont;

	output finish,load_n,load_result, sel_result,load_continue,stack1_push,stack1_pop,stack2_push,stack2_pop;
	output [1:0] sel_n, sel_stack1;
	output [1:0] sel_continue;
	output [7:0] state;

	reg [7:0] state, next_state;

	always @(posedge clk)
	begin
		if(rst)
			state = 8'd0;
		else
			state = next_state;
	end
	assign finish = (state == 8'd8) ? 1 : 0;	
	assign sel_continue = (state == 8'd3) ? 2'd0 :
			      (state == 8'd5) ? 2'd1 :
			      (state == 8'd0) ? 2'd2 :
			      (state == 8'd6) ? 2'd3 :2'd3;
	
	assign load_continue = (state==8'd0||state==8'd3||state==8'd5||state==8'd6) ? 1:0;

	assign sel_n = (state == 8'd0) ? 2'd0:
			(state == 8'd5) ? 2'd1:
			(state == 8'd3) ? 2'd2:2'd2;
	assign load_n = (state==8'd0||state==8'd3||state==8'd5)?1:0;

	assign sel_stack1 = (state == 8'd2) ? 1:	
			    (state == 8'd3) ? 2:2;     
	assign stack1_push = (state==8'd2 ||state==8'd3)?1 :0;
	assign stack1_pop = (state==8'd5||state==8'd6)? 1 : 0;

	assign sel_result = (state == 8'd7)? 0:
			    (state==8'd4)?1:0;
	assign load_result = (state==8'd7||state==8'd4 ) ? 1 : 0;
	   
	assign stack2_push = (state==8'd5)?1 : 0;
	assign stack2_pop = (state == 8'd7)? 1 : 0;
	

	

	
	always @(state or start or nless2 or cont)
	begin
		case(state)
			8'd0: if(start)
				next_state = 8'd1;
			      else
				next_state = 8'd0;
			8'd1: if(nless2) 
				next_state = 8'd4;
			      else
				next_state = 8'd2;
			8'd2:
				next_state = 8'd3;
			8'd3:
				next_state = 8'd1;
			8'd4:
				next_state =cont;
			8'd5:
				next_state = 8'd1;
			8'd6: 
				next_state=   8'd7;
			8'd7:
				next_state = cont;
			8'd8:
				next_state = 8'd8;
			default: next_state = 8'd0;
		endcase
	end
	
endmodule
*/
