// Digital circuit stack.dig as structural Verilog
module stack (
  input  clk,
  input  rst,
  input  push,
  input  pop,
  input  [7:0] din,
  output empty,
  output full,
  output [7:0] dout,
  output [7:0] top_num
);

  stack8 #(.applicationType("IVERILOG")) u_stack8 (
    .clk(clk), .rst(rst), .push(push), .pop(pop), .din(din), .empty(empty), .full(full), .dout(dout),
    .top_num(top_num));
endmodule

/* Code of stack8:
module stack8(clk, rst, push, pop, din, empty, full, dout,top_num);
	input clk, rst, push, pop;
	input [7:0] din;
	output empty, full;
	output [7:0] dout;
	output [7:0] top_num;

	reg [7:0] data[0:255];
	reg [7:0] top;
		
	assign dout = data[top];
	assign empty = (top == 8'd0)? 1:0;
	assign full = (top == 8'd255)? 1:0;
	assign top_num=data[top];
	always @(posedge clk)
	begin
		if(rst)
			top = 8'd0;
		else if(push)
		begin
			top = top + 1;
			data[top] = din;
		end
		else if(pop)
		begin
			top = top - 1;
		end
	end
	
endmodule
*/
