// Digital circuit alu.dig as structural Verilog
module alu (
  input  [31:0] a,
  input  [31:0] b,
  input  [3:0] aluOp,
  input  shamt,
  output [31:0] c
);

  wire add_1_s, comparator_1_eq, comparator_2_eq, multiplexer_2_out;
  wire [0:0] slt_lt, sltu_lt;
  wire [31:0] add_2_s, and_1_out, barrelshifter_1_out, barrelshifter_2_out, bitextender_1_out,
       multiplexer_1_out, multiplexer_3_out, multiplexer_4_out, or_1_out, sll_out, sub_1_s, xor_1_out;

  Comparator #(.Bits(3)) comparator_1 (.a(aluOp[2:0]), .b(3'b001), .eq(comparator_1_eq));  // open: gt, lt
  Comparator #(.Bits(3)) comparator_2 (.a(aluOp[2:0]), .b(3'b101), .eq(comparator_2_eq));  // open: gt, lt
  Add add_1 (.a(comparator_1_eq), .b(comparator_2_eq), .c_i(1'b0), .s(add_1_s));  // open: c_o
  BitExtender #(.inputBits(5), .outputBits(32)) bitextender_1 (.in(b[4:0]), .out(bitextender_1_out));
  Multiplexer #(.Bits(32)) multiplexer_1 (
    .sel(multiplexer_2_out), .in_0(b), .in_1(bitextender_1_out), .out(multiplexer_1_out));
  Multiplexer multiplexer_2 (.sel(shamt), .in_0(1'b0), .in_1(add_1_s), .out(multiplexer_2_out));
  Add #(.Bits(32)) add_2 (.a(a), .b(multiplexer_1_out), .c_i(1'b0), .s(add_2_s));  // open: c_o
  Sub #(.Bits(32)) sub_1 (.a(a), .b(multiplexer_1_out), .c_i(1'b0), .s(sub_1_s));  // open: c_o
  Comparator #(.Signed("true"), .Bits(32)) slt (.a(a), .b(multiplexer_1_out), .lt(slt_lt[0]));  // open: gt, eq
  Comparator #(.Bits(32)) sltu (.a(a), .b(multiplexer_1_out), .lt(sltu_lt[0]));  // open: gt, eq
  assign xor_1_out = a ^ multiplexer_1_out;  // XOr xor_1, 32 bits wide
  BarrelShifter #(.Bits(32), .direction("right")) barrelshifter_1 (
    .in(a), .shift(multiplexer_1_out[5:0]), .out(barrelshifter_1_out));
  BarrelShifter #(.Bits(32), .barrelShifterMode("arithmetic"), .direction("right")) barrelshifter_2 (
    .in(a), .shift(multiplexer_1_out[5:0]), .out(barrelshifter_2_out));
  assign or_1_out = a | multiplexer_1_out;  // Or or_1, 32 bits wide
  assign and_1_out = a & multiplexer_1_out;  // And and_1, 32 bits wide
  Multiplexer #(.Bits(32)) multiplexer_3 (.sel(aluOp[3]), .in_0(add_2_s), .in_1(sub_1_s), .out(multiplexer_3_out));
  BarrelShifter #(.Bits(32)) sll (.in(a), .shift(multiplexer_1_out[5:0]), .out(sll_out));
  Multiplexer #(.Bits(32)) multiplexer_4 (
    .sel(aluOp[3]), .in_0(barrelshifter_1_out), .in_1(barrelshifter_2_out), .out(multiplexer_4_out));
  Multiplexer #(.Selector_Bits(3), .Bits(32)) multiplexer_5 (
    .sel(aluOp[2:0]), .in_0(multiplexer_3_out), .in_1(sll_out), .in_2({{31{1'b0}}, slt_lt[0]}),
    .in_3({{31{1'b0}}, sltu_lt[0]}), .in_4(xor_1_out), .in_5(multiplexer_4_out), .in_6(or_1_out),
    .in_7(and_1_out), .out(c));
endmodule
