// Digital circuit alu_b.dig as structural Verilog
module alu_b (
  input  [6:0] imm,
  input  [31:0] rs1,
  input  [31:0] rs2,
  input  [4:0] rd,
  input  [31:0] pc,
  input  [3:0] aluop,
  output [31:0] pc2
);

  wire add_1_s, add_3_s, comparator_1_eq, comparator_1_gt, comparator_1_lt, comparator_2_eq, comparator_2_gt,
       comparator_2_lt, multiplexer_1_out, not_1_out;
  wire [31:0] bitextender_1_out, multiplexer_2_out;

  Comparator #(.Signed("true"), .Bits(32)) comparator_1 (
    .a(rs1), .b(rs2), .gt(comparator_1_gt), .eq(comparator_1_eq), .lt(comparator_1_lt));
  Comparator #(.Signed("true"), .Bits(32)) comparator_2 (
    .a(rs1), .b(rs2), .gt(comparator_2_gt), .eq(comparator_2_eq), .lt(comparator_2_lt));
  BitExtender #(.inputBits(12), .outputBits(32)) bitextender_1 (
    .in({imm[6], rd[0], imm[5:0], rd[4:1]}), .out(bitextender_1_out));
  Add add_1 (.a(comparator_1_gt), .b(comparator_1_eq), .c_i(1'b0), .s(add_1_s));  // open: c_o
  not not_1 (not_1_out, comparator_1_eq);
  Add #(.Bits(32)) add_2 (.a(multiplexer_2_out), .b(pc), .c_i(1'b0), .s(pc2));  // open: c_o
  Add add_3 (.a(comparator_2_gt), .b(comparator_2_eq), .c_i(1'b0), .s(add_3_s));  // open: c_o
  Multiplexer #(.Selector_Bits(3)) multiplexer_1 (
    .sel(aluop[2:0]), .in_0(comparator_1_eq), .in_1(not_1_out), .in_2(1'b1), .in_3(1'b1),
    .in_4(comparator_1_lt), .in_5(add_1_s), .in_6(comparator_2_lt), .in_7(add_3_s), .out(multiplexer_1_out));
  Multiplexer #(.Bits(32)) multiplexer_2 (
    .sel(multiplexer_1_out), .in_0(32'h1), .in_1(bitextender_1_out), .out(multiplexer_2_out));
endmodule
