// Digital circuit alu_sl.dig as structural Verilog
module alu_sl (
  input  [31:0] rs1,
  input  [11:0] imm,
  input  [3:0] aluOP,
  input  [4:0] rd,
  input  alu,
  output [31:0] value
);

  wire [11:0] multiplexer_1_out;
  wire [31:0] add_1_s, bitextender_1_out, bitextender_2_out, bitextender_3_out;

  Multiplexer #(.Bits(12)) multiplexer_1 (.sel(alu), .in_0(imm), .in_1({imm[11:5], rd}), .out(multiplexer_1_out));
  BitExtender #(.inputBits(12), .outputBits(32)) bitextender_1 (.in(multiplexer_1_out), .out(bitextender_1_out));
  Add #(.Bits(32)) add_1 (.a(rs1), .b(bitextender_1_out), .c_i(1'b0), .s(add_1_s));  // open: c_o
  BitExtender #(.outputBits(32)) bitextender_2 (.in(add_1_s[7:0]), .out(bitextender_2_out));
  BitExtender #(.inputBits(16), .outputBits(32)) bitextender_3 (.in(add_1_s[15:0]), .out(bitextender_3_out));
  Multiplexer #(.Selector_Bits(3), .Bits(32)) multiplexer_2 (
    .sel(aluOP[2:0]), .in_0(bitextender_2_out), .in_1(bitextender_3_out), .in_2(add_1_s), .in_3(32'h1),
    .in_4(bitextender_2_out), .in_5(bitextender_3_out), .in_6(32'h1), .in_7(32'h1), .out(value));
endmodule
