// Digital circuit controller.dig as structural Verilog
module controller (
  input  [6:0] opcode,
  input  [2:0] fun3,
  input  [6:0] fun7,
  output [3:0] aluOp,
  output pc_load,
  output reg_write,
  output ram_load,
  output alu_scrb,
  output [1:0] pc_sel,
  output [1:0] din_sel
);

  wire comparator_1_eq, comparator_2_eq, comparator_3_eq, comparator_4_eq, comparator_5_eq, comparator_6_eq,
       comparator_7_eq, comparator_8_eq, comparator_9_eq;

  Comparator #(.Bits(7)) comparator_1 (.a(opcode), .b(7'b0010011), .eq(comparator_1_eq));  // open: gt, lt
  Comparator #(.Bits(7)) comparator_2 (.a(opcode), .b(7'b0110011), .eq(comparator_2_eq));  // open: gt, lt
  Comparator #(.Bits(7)) comparator_3 (.a(opcode), .b(7'b0100011), .eq(comparator_3_eq));  // open: gt, lt
  Comparator #(.Bits(7)) comparator_4 (.a(opcode), .b(7'b0000011), .eq(comparator_4_eq));  // open: gt, lt
  Comparator #(.Bits(7)) comparator_5 (.a(opcode), .b(7'b1100011), .eq(comparator_5_eq));  // open: gt, lt
  Comparator #(.Bits(7)) comparator_6 (.a(opcode), .b(7'b1101111), .eq(comparator_6_eq));  // open: gt, lt
  Comparator #(.Bits(7)) comparator_7 (.a(opcode), .b(7'b1100111), .eq(comparator_7_eq));  // open: gt, lt
  Comparator #(.Bits(7)) comparator_8 (.a(opcode), .b(7'b0110111), .eq(comparator_8_eq));  // open: gt, lt
  Comparator #(.Bits(7)) comparator_9 (.a(opcode), .b(7'b0010111), .eq(comparator_9_eq));  // open: gt, lt
  d #(.applicationType("IVERILOG")) u_d (
    .d1(comparator_1_eq), .d2(comparator_2_eq), .d3(comparator_3_eq), .d4(comparator_4_eq),
    .d5(comparator_5_eq), .d6(comparator_6_eq), .d7(comparator_7_eq), .d8(comparator_8_eq),
    .d9(comparator_9_eq), .reg_write(reg_write), .ram_load(ram_load), .r1(alu_scrb), .pc_sel(pc_sel),
    .din_sel(din_sel));

  assign aluOp = {fun7[5], fun3};
  assign pc_load = 1'b1;
endmodule

/* Code of d:
module d(d1,d2,d3,d4,d5,d6,d7,d8,d9,reg_write,r1,pc_sel,din_sel,ram_load);
	input d1, d2, d3, d4, d5, d6, d7, d8, d9;
	output reg_write,ram_load;
	output r1;
	output [1:0] pc_sel,din_sel;
	assign reg_write = (d3 == 1 || d5 == 1) ? 0 : 1;
	assign pc_sel = (d5 == 1) ? 1 :
			(d6 == 1) ? 2 :
			(d7 == 1) ? 3 : 0;
	assign r1 = (d2 == 1 || d3 == 1 || d5 == 1) ? 0 : 1;
	assign din_sel = (d4 == 1) ? 1 :
			(d6 == 1 || d7 == 1) ? 2 :
			(d8 == 1 || d9 == 1) ? 3 : 0;
	assign ram_load = (d3 == 1 || d4 == 1) ? 1 : 0;

endmodule
*/
