// Digital circuit pc.dig as structural Verilog
module pc (
  input  clk,
  input  rst,
  input  load,
  input  [31:0] din,
  output [31:0] dout
);

  pc #(.applicationType("IVERILOG")) u_pc (.clk(clk), .rst(rst), .load(load), .din(din), .dout(dout));
endmodule

/* Code of pc:
module pc(clk, rst, load, din, dout);
	input clk, rst, load;
	input [31:0] din;

	output [31:0] dout;

	reg [31:0] d;

	assign dout = d;

	always @(posedge clk)
	begin
		if (rst)
			d = 0;
		else if(load)
			d = din;
	end

endmodule
*/
