// Digital circuit regfile.dig as structural Verilog
module regfile (
  input  clk,
  input  [4:0] rs1,
  input  [4:0] rs2,
  input  [4:0] rd,
  input  [31:0] din,
  input  we,
  output [31:0] r1,
  output [31:0] r2
);

  regfile #(.applicationType("IVERILOG")) u_regfile (
    .clk(clk), .we(we), .rs1(rs1), .rs2(rs2), .rd(rd), .din(din), .r1(r1), .r2(r2));
endmodule

/* Code of regfile:
module regfile(clk, we, rs1, rs2, rd, din, r1, r2);
	input clk, we;
	input [4:0] rs1, rs2, rd;
	input [31:0] din;
	output [31:0] r1, r2;

	reg [31:0] d[31:0];

	assign r1 = (rs1 == 0) ? 0 : d[rs1];
	assign r2 = (rs2 == 0) ? 0 : d[rs2];

	always @(posedge clk)
	begin
		if (we)
			d[rd] = din;
	end
endmodule
*/
