// Digital circuit work.dig as structural Verilog
module work (
  input  clk,
  input  rst
);

  wire controller_1_alu_scrb, controller_1_pc_load, controller_1_ram_load, controller_1_reg_write;
  wire [0:0] add_1_s;
  wire [1:0] controller_1_din_sel, controller_1_pc_sel;
  wire [3:0] controller_1_aluop;
  wire [4:0] CODE_d_2;
  wire [6:0] CODE_d;
  wire [19:0] barrelshifter_1_out, barrelshifter_2_out, CODE_d_3;
  wire [30:0] add_1_s_2;
  wire [31:0] add_2_s, add_3_s, add_4_s, alu_1_c, alu_b_1_pc2, alu_sl_1_value, bitextender_1_out,
       bitextender_2_out, bitextender_3_out, bitextender_4_out, bitextender_5_out, bitextender_6_out,
       multiplexer_1_out, multiplexer_2_out, multiplexer_3_out, multiplexer_4_out, multiplexer_5_out,
       pc_1_dout, ramdualport_1_d, regfile_1_r1, regfile_1_r2;

  BitExtender #(.inputBits(12), .outputBits(32)) bitextender_1 (.in(CODE_d_3[19:8]), .out(bitextender_1_out));
  BitExtender #(.inputBits(20), .outputBits(32)) bitextender_2 (.in(CODE_d_3), .out(bitextender_2_out));
  Add #(.Bits(32)) add_1 (
    .a(bitextender_1_out), .b(regfile_1_r1), .c_i(1'b0), .s({add_1_s_2, add_1_s[0]}));  // open: c_o
  BarrelShifter #(.Bits(20)) barrelshifter_1 (.in(CODE_d_3), .shift(5'b01100), .out(barrelshifter_1_out));
  BarrelShifter #(.Bits(20)) barrelshifter_2 (.in(CODE_d_3), .shift(5'b01100), .out(barrelshifter_2_out));
  Add #(.Bits(32)) add_2 (.a(bitextender_2_out), .b(add_4_s), .c_i(1'b0), .s(add_2_s));  // open: c_o
  BitExtender #(.inputBits(20), .outputBits(32)) bitextender_3 (.in(barrelshifter_2_out), .out(bitextender_3_out));
  Add #(.Bits(32)) add_3 (.a(pc_1_dout), .b(bitextender_3_out), .c_i(1'b0), .s(add_3_s));  // open: c_o
  Multiplexer #(.Selector_Bits(2), .Bits(32)) multiplexer_1 (
    .sel(controller_1_pc_sel), .in_0(add_4_s), .in_1(alu_b_1_pc2), .in_2(add_2_s), .in_3({add_1_s_2, 1'b0}),
    .out(multiplexer_1_out));
  Multiplexer #(.Bits(32)) multiplexer_2 (
    .sel(CODE_d[5]), .in_0(add_3_s), .in_1({barrelshifter_1_out, {12{1'b0}}}), .out(multiplexer_2_out));
  pc pc_1 (.clk(clk), .rst(rst), .load(controller_1_pc_load), .din(multiplexer_1_out), .dout(pc_1_dout));
  Add #(.Bits(32)) add_4 (.a(pc_1_dout), .b(32'h1), .c_i(1'b0), .s(add_4_s));  // open: c_o
  ROM #(.AddrBits(24), .Bits(32)) CODE (.A(pc_1_dout[23:0]), .sel(1'b1), .D({CODE_d_3, CODE_d_2, CODE_d}));
  Multiplexer #(.Selector_Bits(2), .Bits(32)) multiplexer_3 (
    .sel(controller_1_din_sel), .in_0(alu_1_c), .in_1(multiplexer_5_out), .in_2(add_4_s),
    .in_3(multiplexer_2_out), .out(multiplexer_3_out));
  BitExtender #(.inputBits(12), .outputBits(32)) bitextender_4 (.in(CODE_d_3[19:8]), .out(bitextender_4_out));
  controller controller_1 (
    .opcode(CODE_d), .fun3(CODE_d_3[2:0]), .fun7(CODE_d_3[19:13]), .aluOp(controller_1_aluop),
    .pc_load(controller_1_pc_load), .reg_write(controller_1_reg_write), .ram_load(controller_1_ram_load),
    .alu_scrb(controller_1_alu_scrb), .pc_sel(controller_1_pc_sel), .din_sel(controller_1_din_sel));
  regfile regfile_1 (
    .clk(clk), .rs1(CODE_d_3[7:3]), .rs2(CODE_d_3[12:8]), .rd(CODE_d_2), .din(multiplexer_3_out),
    .we(controller_1_reg_write), .r1(regfile_1_r1), .r2(regfile_1_r2));
  Multiplexer #(.Bits(32)) multiplexer_4 (
    .sel(controller_1_alu_scrb), .in_0(regfile_1_r2), .in_1(bitextender_4_out), .out(multiplexer_4_out));
  alu alu_1 (
    .a(regfile_1_r1), .b(multiplexer_4_out), .aluOp(controller_1_aluop), .shamt(controller_1_alu_scrb),
    .c(alu_1_c));
  alu_sl alu_sl_1 (
    .rs1(regfile_1_r1), .imm(CODE_d_3[19:8]), .aluOP(controller_1_aluop), .rd(CODE_d_2), .alu(CODE_d[5]),
    .value(alu_sl_1_value));
  alu_b alu_b_1 (
    .imm(CODE_d_3[19:13]), .rs1(regfile_1_r1), .rs2(multiplexer_4_out), .rd(CODE_d_2), .pc(pc_1_dout),
    .aluop(controller_1_aluop), .pc2(alu_b_1_pc2));
  RAMDualPort #(.AddrBits(24), .Bits(32)) ramdualport_1 (
    .A(alu_sl_1_value[23:0]), .Din(regfile_1_r2), .str(controller_1_ram_load), .C(clk), .ld(1'b1),
    .D(ramdualport_1_d));
  BitExtender #(.outputBits(32)) bitextender_5 (.in(ramdualport_1_d[7:0]), .out(bitextender_5_out));
  BitExtender #(.inputBits(16), .outputBits(32)) bitextender_6 (.in(ramdualport_1_d[15:0]), .out(bitextender_6_out));
  Multiplexer #(.Selector_Bits(3), .Bits(32)) multiplexer_5 (
    .sel(controller_1_aluop[2:0]), .in_0(bitextender_5_out), .in_1(bitextender_6_out),
    .in_2(ramdualport_1_d), .in_3(32'h1), .in_4({{24{1'b0}}, ramdualport_1_d[7:0]}),
    .in_5({{16{1'b0}}, ramdualport_1_d[15:0]}), .in_6(32'h1), .in_7(32'h1), .out(multiplexer_5_out));

  // Notes on the sheet:
  //   CODE loads ROM
endmodule
